# Fritzing sketch Amplificatore 1W (saved by Fritzing 0.9.1b)
circuit board: 4.27698cm x 3.50966cm
breadboards: 1

parts:
  IC1 = FRM050 [package=THT]
  C1 = Electrolytic Capacitor [capacitance=1µF package="100 mil [THT, electrolytic]"]
  R1 = Resistor [tolerance=±5% resistance=220 package=THT]
  C3 = Tantalum Capacitor [capacitance=100pF package="A 3216 [SMD, tantalum]"]
  C4 = Electrolytic Capacitor [capacitance=4.7µF voltage=10V package="100 mil [THT, electrolytic]"]
  R1_2 = Resistor [tolerance=±5% resistance=220 package=THT]
  C5 = Tantalum Capacitor [capacitance=100pF package="A 3216 [SMD, tantalum]"]
  U1 = 3.5mm Audio Jack [package=audio-jack]
  U2 = 3.5mm Audio Jack [package=audio-jack]
  R2 = Resistor [tolerance=±5% resistance=220 package=THT]
  R2_2 = Resistor [tolerance=±5% resistance=220 package=THT]
  C9 = Electrolytic Capacitor [capacitance=1µF package="100 mil [THT, electrolytic]"]
  R5 = Resistor [tolerance=±5% resistance=220 package=THT]
  R5_2 = Resistor [tolerance=±5% resistance=220 package=THT]
  R7 = Resistor [tolerance=±5% resistance=220 package=THT]
  R7_2 = Resistor [tolerance=±5% resistance=220 package=THT]
  C7 = Tantalum Capacitor [capacitance=1μF package="A 3216 [SMD, tantalum]"]
  VCC1 = Battery
  C8 = Electrolytic Capacitor [capacitance=1µF package="100 mil [THT, electrolytic]"]
  C2 = Electrolytic Capacitor [capacitance=47µF voltage=10V package="100 mil [THT, electrolytic]"]
  C6 = Tantalum Capacitor [capacitance=1μF package="A 3216 [SMD, tantalum]"]

nets:
  N1: IC1.+V, C4.+
  N2: IC1.In_6, C1.+, VCC1.+
  N3: IC1.In_5, C2.+
  N4: IC1.In_4, C1.-, C3.-, C5.-, U1.SLEEVE, U2.SLEEVE, C9.-, R5.Pin_1, R5_2.Pin_1, R7.Pin_1, R7_2.Pin_1, VCC1.-, C8.-
  N5: IC1.Out_6, C9.+
  N6: IC1.In_7, R2.Pin_0, R5_2.Pin_0, C6.-
  N7: IC1.Out_4, R2_2.Pin_0, R5.Pin_0, C7.-
  N8: IC1.0V, C8.+
  N9: R1.Pin_0, C2.-
  N10: R1.Pin_1, C3.+, U1.RIGHT
  N11: C4.-, R1_2.Pin_0
  N12: R1_2.Pin_1, C5.+, U1.LEFT
  N13: U2.RIGHT, R2.Pin_1, R7_2.Pin_0, C6.+
  N14: U2.LEFT, R2_2.Pin_1, R7.Pin_0, C7.+

notes:
  Amplificatore
  1W
  OUT
  IN
