# Fritzing sketch Display (saved by Fritzing 0.9.2b)
circuit board: 15.3cm x 4.1cm
breadboards: 1

parts:
  7_Segment2 = 7-Segment LED Display [package=THT]
  7_Segment3 = 7-Segment LED Display [package=THT]
  7_Segment5 = 7-Segment LED Display [package=THT]
  7_Segment4 = 7-Segment LED Display [package=THT]
  7_Segment8 = 7-Segment LED Display [package=THT]
  7_Segment1 = 7-Segment LED Display [package=THT]
  7_Segment6 = 7-Segment LED Display [package=THT]
  7_Segment7 = 7-Segment LED Display [package=THT]
  J2 = female pin header, 16 pins [form="♀ (female)"]

nets:
  N1: 7_Segment2.cathodeE, 7_Segment3.cathodeE, 7_Segment5.cathodeE, 7_Segment4.cathodeE, 7_Segment8.cathodeE, 7_Segment1.cathodeE, 7_Segment6.cathodeE, 7_Segment7.cathodeE, J2.pin5
  N2: 7_Segment2.cathodeD, 7_Segment3.cathodeD, 7_Segment5.cathodeD, 7_Segment4.cathodeD, 7_Segment8.cathodeD, 7_Segment1.cathodeD, 7_Segment6.cathodeD, 7_Segment7.cathodeD, J2.pin6
  N3: 7_Segment2.cathodeC, 7_Segment3.cathodeC, 7_Segment5.cathodeC, 7_Segment4.cathodeC, 7_Segment8.cathodeC, 7_Segment1.cathodeC, 7_Segment6.cathodeC, 7_Segment7.cathodeC, J2.pin7
  N4: 7_Segment2.cathodeDP, 7_Segment3.cathodeDP, 7_Segment5.cathodeDP, 7_Segment4.cathodeDP, 7_Segment8.cathodeDP, 7_Segment1.cathodeDP, 7_Segment6.cathodeDP, 7_Segment7.cathodeDP, J2.pin8
  N5: 7_Segment2.cathodeB, 7_Segment3.cathodeB, 7_Segment5.cathodeB, 7_Segment4.cathodeB, 7_Segment8.cathodeB, 7_Segment1.cathodeB, 7_Segment6.cathodeB, 7_Segment7.cathodeB, J2.pin4
  N6: 7_Segment2.cathodeA, 7_Segment3.cathodeA, 7_Segment5.cathodeA, 7_Segment4.cathodeA, 7_Segment8.cathodeA, 7_Segment1.cathodeA, 7_Segment6.cathodeA, 7_Segment7.cathodeA, J2.pin3
  N7: 7_Segment2.commAnode#7, J2.pin10
  N8: 7_Segment2.cathodeF, 7_Segment3.cathodeF, 7_Segment5.cathodeF, 7_Segment4.cathodeF, 7_Segment8.cathodeF, 7_Segment1.cathodeF, 7_Segment6.cathodeF, 7_Segment7.cathodeF, J2.pin2
  N9: 7_Segment2.cathodeG, 7_Segment3.cathodeG, 7_Segment5.cathodeG, 7_Segment4.cathodeG, 7_Segment8.cathodeG, 7_Segment1.cathodeG, 7_Segment6.cathodeG, 7_Segment7.cathodeG, J2.pin1
  N10: 7_Segment3.commAnode#7, J2.pin11
  N11: 7_Segment5.commAnode#7, J2.pin12
  N12: 7_Segment4.commAnode#7, J2.pin13
  N13: 7_Segment8.commAnode#7, J2.pin16
  N14: 7_Segment1.commAnode#7, J2.pin9
  N15: 7_Segment6.commAnode#7, J2.pin14
  N16: 7_Segment7.commAnode#7, J2.pin15

notes:
  EletroLaix
